# Fritzing sketch lo_l293d (saved by Fritzing 0.9.1b)
breadboards: 1

parts:
  元件2 = LinkIt ONE
  IC1 = L293D [package=THT]
  VCC1 = Battery
  M1 = DC Motor
  M2 = DC Motor

nets:
  N1: 元件2.~D3/4, IC1.Enable_1
  N2: 元件2.D4/5, IC1.In_1
  N3: 元件2.D5/6, IC1.In_2
  N4: 元件2.D6/7, IC1.In_3
  N5: 元件2.D7/8, IC1.In_4
  N6: 元件2.~D9/10, IC1.Enable_2
  N7: 元件2.GND/26, IC1.0V, VCC1.-
  N8: 元件2.5V/28, IC1.+V
  N9: IC1.Out_1_(_Controlled_by_Enable_1_), M1.pin_1
  N10: IC1.Out_2_(_Controlled_by_Enable_1_), M1.pin_2
  N11: IC1.+Vmotor, VCC1.+
  N12: IC1.Out_3_(_Controlled_by_Enable_2_), M2.pin_1
  N13: IC1.Out_4_(_Controlled_by_Enable_2_), M2.pin_2

custom parts:
  LinkIt ONE: Seeed Studio Shield LinkIt ONE board

// code stored in the sketch: Linkit.ino

